# Fritzing sketch Trilly (saved by Fritzing 0.9.3b)
breadboards: 1

parts:
  ARDUINO_MINI_PRO = Arduino Pro Mini v13
  LED1 = LED - 5mm [color="Yellow (595nm)" current=15mA package="5 mm [THT]"]
  LED2 = LED - 5mm [color="Yellow (595nm)" current=15mA package="5 mm [THT]"]
  LED3 = LED - 5mm [color="White (4500K)" current=22mA package="5 mm [THT]"]
  R1 = Resistor [tolerance=±5% resistance=100 package=THT]
  R2 = Resistor [tolerance=±5% resistance=100 package=THT]
  Power_plug1 = Power plug  # not connected
  V1 = DC Power [voltage=12V]

nets (from the schematic view):
  N1: ARDUINO_MINI_PRO.GND, LED2.cathode, LED3.cathode, V1.V-
  N2: ARDUINO_MINI_PRO.RAW, V1.V+
  N3: ARDUINO_MINI_PRO.D6_PWM, LED3.anode
  N4: ARDUINO_MINI_PRO.D5_PWM, R2.Pin_0
  N5: ARDUINO_MINI_PRO.D3_PWM, R1.Pin_0
  N6: LED1.anode, R1.Pin_1
  N7: LED2.anode, R2.Pin_1
